// Logisim project ex2.circ as structural Verilog: 1 circuit, main circuit main
module main (
  input  in_1
);

  wire and_1_out, and_2_out, button_1_out, clock_1_out, j_k_ff_1_q, j_k_ff_2_q, not_1_out, xor_1_out;

  not not_1 (not_1_out, in_1);
  and and_1 (and_1_out, j_k_ff_2_q, in_1);
  xor xor_1 (xor_1_out, j_k_ff_2_q, in_1);
  Clock clock_1 (.out(clock_1_out));
  J_K_Flip_Flop j_k_ff_1 (
    .J(and_1_out), .clk(xor_1_out), .K(clock_1_out), .Q(j_k_ff_1_q), .en(button_1_out));  // open: Qn, preset, reset
  J_K_Flip_Flop j_k_ff_2 (
    .J(not_1_out), .clk(in_1), .K(clock_1_out), .Q(j_k_ff_2_q), .en(button_1_out));  // open: Qn, preset, reset
  Button button_1 (.out(button_1_out));
  LED led_1 (.in(j_k_ff_1_q));
  LED led_2 (.in(j_k_ff_2_q));
  LED led_3 (.in(and_2_out));
  and and_2 (and_2_out, j_k_ff_1_q, j_k_ff_2_q);
endmodule
