// Logisim project ex01.circ as structural Verilog: 1 circuit, main circuit main
module main (
  input  in_1,
  input  Enable,
  input  Clear,
  output out_4,
  output out_5,
  output out_6,
  output out_7
);

  wire clock_1_out, j_k_ff_1_qn, j_k_ff_2_qn, j_k_ff_3_qn, not_1_out;

  Clock clock_1 (.out(clock_1_out));
  not not_1 (not_1_out, in_1);
  J_K_Flip_Flop j_k_ff_1 (
    .J(in_1), .clk(clock_1_out), .K(not_1_out), .Q(out_4), .Qn(j_k_ff_1_qn), .en(Enable), .reset(Clear));  // open: preset
  J_K_Flip_Flop j_k_ff_2 (
    .J(out_4), .clk(clock_1_out), .K(j_k_ff_1_qn), .Q(out_5), .Qn(j_k_ff_2_qn), .en(Enable), .reset(Clear));  // open: preset
  J_K_Flip_Flop j_k_ff_3 (
    .J(out_5), .clk(clock_1_out), .K(j_k_ff_2_qn), .Q(out_6), .Qn(j_k_ff_3_qn), .en(Enable), .reset(Clear));  // open: preset
  J_K_Flip_Flop j_k_ff_4 (
    .J(out_6), .clk(clock_1_out), .K(j_k_ff_3_qn), .Q(out_7), .en(Enable), .reset(Clear));  // open: Qn, preset
endmodule
