// Logisim project ex02.circ as structural Verilog: 1 circuit, main circuit main
module main (
  input  \input ,
  input  clear,
  input  on,
  output out_4,
  output out_5,
  output out_6,
  output out_7,
  output out_8,
  output out_9
);

  wire clock_1_out, j_k_ff_1_qn, j_k_ff_2_qn, j_k_ff_3_qn, j_k_ff_4_qn, j_k_ff_5_qn;

  Clock clock_1 (.out(clock_1_out));
  J_K_Flip_Flop j_k_ff_1 (
    .J(\input ), .clk(clock_1_out), .K(\input ), .Q(out_9), .Qn(j_k_ff_1_qn), .en(on), .reset(clear));  // open: preset
  J_K_Flip_Flop j_k_ff_2 (
    .J(\input ), .clk(j_k_ff_1_qn), .K(\input ), .Q(out_8), .Qn(j_k_ff_2_qn), .en(on), .reset(clear));  // open: preset
  J_K_Flip_Flop j_k_ff_3 (
    .J(\input ), .clk(j_k_ff_2_qn), .K(\input ), .Q(out_7), .Qn(j_k_ff_3_qn), .en(on), .reset(clear));  // open: preset
  J_K_Flip_Flop j_k_ff_4 (
    .J(\input ), .clk(j_k_ff_3_qn), .K(\input ), .Q(out_6), .Qn(j_k_ff_4_qn), .en(on), .reset(clear));  // open: preset
  J_K_Flip_Flop j_k_ff_5 (
    .J(\input ), .clk(j_k_ff_4_qn), .K(\input ), .Q(out_5), .Qn(j_k_ff_5_qn), .en(on), .reset(clear));  // open: preset
  J_K_Flip_Flop j_k_ff_6 (
    .J(\input ), .clk(j_k_ff_5_qn), .K(\input ), .Q(out_4), .en(on), .reset(clear));  // open: Qn, preset
endmodule
