// Logisim project ex04.circ as structural Verilog: 1 circuit, main circuit main
module main (
  input  \input ,
  output out_2,
  output out_3,
  output out_4,
  output out_5,
  output out_6
);

  wire and_1_out, clock_1_out, not_1_out, not_2_out;

  Clock clock_1 (.out(clock_1_out));
  J_K_Flip_Flop j_k_ff_1 (
    .J(\input ), .clk(clock_1_out), .K(\input ), .Q(out_6), .preset(and_1_out));  // open: Qn, en, reset
  and and_1 (and_1_out, out_6, not_1_out, out_4, not_2_out);
  J_K_Flip_Flop j_k_ff_2 (.J(\input ), .clk(out_6), .K(\input ), .Q(out_5), .preset(and_1_out));  // open: Qn, en, reset
  not not_1 (not_1_out, out_5);
  not not_2 (not_2_out, out_3);
  J_K_Flip_Flop j_k_ff_3 (.J(\input ), .clk(out_5), .K(\input ), .Q(out_4), .preset(and_1_out));  // open: Qn, en, reset
  J_K_Flip_Flop j_k_ff_4 (.J(\input ), .clk(out_4), .K(\input ), .Q(out_3), .preset(and_1_out));  // open: Qn, en, reset
  J_K_Flip_Flop j_k_ff_5 (.clk(out_3), .Q(out_2), .reset(and_1_out));  // open: J, K, Qn, preset, en

  // Notes on the sheet:
  //   Pedido com 5 bits, mantive o ultimo bit em 0, para n alterar a saida
endmodule
