// Logisim project ex05.circ as structural Verilog: 1 circuit, main circuit main
module main (
  input  \input ,
  input  in_2,
  output out_3,
  output Saida,
  output out_5
);

  wire and_1_out, clock_1_out, or_1_out, t_ff_1_qn, t_ff_2_qn;

  Clock clock_1 (.out(clock_1_out));
  or or_1 (or_1_out, in_2, and_1_out);
  T_Flip_Flop t_ff_1 (.clk(clock_1_out), .T(\input ), .Q(out_5), .Qn(t_ff_1_qn), .reset(or_1_out));  // open: preset, en
  T_Flip_Flop t_ff_2 (.clk(t_ff_1_qn), .T(\input ), .Q(Saida), .Qn(t_ff_2_qn), .reset(or_1_out));  // open: preset, en
  and and_1 (and_1_out, Saida, out_5, out_3);
  T_Flip_Flop t_ff_3 (.clk(t_ff_2_qn), .T(\input ), .Q(out_3), .reset(or_1_out));  // open: Qn, preset, en
endmodule
