// Logisim project ex6.circ as structural Verilog: 1 circuit, main circuit main
module main (
  input  reset,
  input  \input ,
  input  input_2,
  output out_4,
  output out_5,
  output out_6,
  output out_7,
  output out_8,
  output out_9
);

  wire clock_1_out, clock_2_out, d_ff_1_q, d_ff_2_q, d_ff_3_q, j_k_ff_1_qn, not_1_out, not_2_out, not_3_out,
       not_4_out, not_5_out, not_6_out, or_1_out, or_2_out;

  Clock clock_1 (.out(clock_1_out));
  or or_1 (or_1_out, \input , out_9);
  J_K_Flip_Flop j_k_ff_1 (
    .J(or_1_out), .clk(clock_1_out), .K(not_1_out), .Q(out_4), .Qn(j_k_ff_1_qn), .reset(reset));  // open: preset, en
  not not_1 (not_1_out, or_1_out);
  Clock clock_2 (.out(clock_2_out));
  or or_2 (or_2_out, input_2, d_ff_3_q);
  not not_2 (not_2_out, out_4);
  D_Flip_Flop d_ff_1 (.clk(clock_2_out), .D(or_2_out), .Q(d_ff_1_q));  // open: Qn, preset, en, reset
  J_K_Flip_Flop j_k_ff_2 (.J(out_4), .clk(clock_1_out), .K(not_2_out), .Q(out_5));  // open: Qn, preset, en, reset
  not not_3 (not_3_out, out_5);
  D_Flip_Flop d_ff_2 (.clk(clock_2_out), .D(d_ff_1_q), .Q(d_ff_2_q));  // open: Qn, preset, en, reset
  J_K_Flip_Flop j_k_ff_3 (.J(out_5), .clk(clock_1_out), .K(not_3_out), .Q(out_6));  // open: Qn, preset, en, reset
  not not_4 (not_4_out, out_6);
  D_Flip_Flop d_ff_3 (.clk(clock_2_out), .D(d_ff_2_q), .Q(d_ff_3_q));  // open: Qn, preset, en, reset
  J_K_Flip_Flop j_k_ff_4 (.J(out_6), .clk(clock_1_out), .K(not_4_out), .Q(out_7));  // open: Qn, preset, en, reset
  J_K_Flip_Flop j_k_ff_5 (.J(out_7), .clk(clock_1_out), .K(not_5_out), .Q(out_8));  // open: Qn, preset, en, reset
  not not_5 (not_5_out, out_7);
  J_K_Flip_Flop j_k_ff_6 (.J(out_8), .clk(clock_1_out), .K(not_6_out), .Q(out_9));  // open: Qn, preset, en, reset
  not not_6 (not_6_out, out_8);
endmodule
