// Logisim project ex03.circ as structural Verilog: 1 circuit, main circuit main
module main (
  input  inp,
  input  clr,
  output out_3,
  output out_4,
  output out_5,
  output out_6,
  output out_7
);

  wire clock_1_out, or_1_out, or_2_out, or_3_out, or_4_out, or_5_out;

  Clock clock_1 (.out(clock_1_out));
  or or_1 (or_1_out, out_3, out_7);
  or or_2 (or_2_out, out_3, out_4);
  J_K_Flip_Flop j_k_ff_1 (
    .J(or_1_out), .clk(clock_1_out), .K(or_1_out), .Q(out_3), .preset(inp), .reset(clr));  // open: Qn, en
  or or_3 (or_3_out, out_4, out_5);
  J_K_Flip_Flop j_k_ff_2 (
    .J(or_2_out), .clk(clock_1_out), .K(or_2_out), .Q(out_4), .reset(clr));  // open: Qn, preset, en
  J_K_Flip_Flop j_k_ff_3 (
    .J(or_3_out), .clk(clock_1_out), .K(or_3_out), .Q(out_5), .reset(clr));  // open: Qn, preset, en
  or or_4 (or_4_out, out_5, out_6);
  J_K_Flip_Flop j_k_ff_4 (
    .J(or_4_out), .clk(clock_1_out), .K(or_4_out), .Q(out_6), .reset(clr));  // open: Qn, preset, en
  or or_5 (or_5_out, out_6, out_7);
  J_K_Flip_Flop j_k_ff_5 (
    .J(or_5_out), .clk(clock_1_out), .K(or_5_out), .Q(out_7), .reset(clr));  // open: Qn, preset, en

  // Notes on the sheet:
  //   Para a direita e circular, uma vez que ao chegar no final, ele retorna para a primeira posição
endmodule
