// Logisim project ex07.circ as structural Verilog: 1 circuit, main circuit main
module main (
  input  inp,
  input  clr,
  output out_3,
  output out_4,
  output out_5,
  output out_6,
  output out_7,
  output out_8
);

  wire clock_1_out, d_ff_1_q, not_1_out, or_1_out, xor_1_out, xor_2_out, xor_3_out, xor_4_out, xor_5_out;

  Clock clock_1 (.out(clock_1_out));
  xor xor_1 (xor_1_out, out_7, out_8);
  D_Flip_Flop d_ff_1 (.clk(clock_1_out), .D(not_1_out), .Q(d_ff_1_q));  // open: Qn, preset, en, reset
  not not_1 (not_1_out, out_8);
  J_K_Flip_Flop j_k_ff_1 (
    .J(xor_1_out), .clk(clock_1_out), .K(xor_1_out), .Q(out_8), .preset(or_1_out), .reset(clr));  // open: Qn, en
  or or_1 (or_1_out, inp, d_ff_1_q);
  xor xor_2 (xor_2_out, out_6, out_7);
  J_K_Flip_Flop j_k_ff_2 (
    .J(xor_2_out), .clk(clock_1_out), .K(xor_2_out), .Q(out_7), .preset(or_1_out), .reset(clr));  // open: Qn, en
  xor xor_3 (xor_3_out, out_5, out_6);
  xor xor_4 (xor_4_out, out_4, out_5);
  J_K_Flip_Flop j_k_ff_3 (
    .J(xor_3_out), .clk(clock_1_out), .K(xor_3_out), .Q(out_6), .preset(or_1_out), .reset(clr));  // open: Qn, en
  xor xor_5 (xor_5_out, out_3, out_4);
  J_K_Flip_Flop j_k_ff_4 (
    .J(xor_4_out), .clk(clock_1_out), .K(xor_4_out), .Q(out_5), .preset(or_1_out), .reset(clr));  // open: Qn, en
  J_K_Flip_Flop j_k_ff_5 (
    .J(xor_5_out), .clk(clock_1_out), .K(xor_5_out), .Q(out_4), .preset(or_1_out), .reset(clr));  // open: Qn, en
  J_K_Flip_Flop j_k_ff_6 (
    .J(out_3), .clk(clock_1_out), .K(out_3), .Q(out_3), .preset(or_1_out), .reset(clr));  // open: Qn, en
endmodule
