// Logisim project ex04.circ as structural Verilog: 1 circuit, main circuit main
module main (
  input  in_1,
  output q3,
  output q2,
  output q1
);

  wire clock_1_out;

  Clock clock_1 (.out(clock_1_out));
  T_Flip_Flop t_ff_1 (.clk(clock_1_out), .T(in_1), .Q(q1));  // open: Qn, preset, reset, en
  T_Flip_Flop t_ff_2 (.clk(q1), .T(in_1), .Q(q2));  // open: Qn, preset, reset, en
  T_Flip_Flop t_ff_3 (.clk(q2), .T(in_1), .Q(q3));  // open: Qn, preset, reset, en
endmodule
