// Logisim project Ex03.circ as structural Verilog: 1 circuit, main circuit main
module main (
  input  a,
  input  b,
  input  c,
  output s
);

  wire multiplexer_1_out, multiplexer_2_out, not_1_out, not_2_out, not_3_out;

  not not_1 (not_1_out, a);
  not not_2 (not_2_out, b);
  not not_3 (not_3_out, c);
  Multiplexer multiplexer_1 (.in0(a), .in1(b), .out(multiplexer_1_out), .sel(not_3_out));  // open: en
  Multiplexer multiplexer_2 (.in0(not_1_out), .in1(not_2_out), .out(multiplexer_2_out), .sel(not_3_out));  // open: en
  Multiplexer multiplexer_3 (.in0(multiplexer_2_out), .in1(multiplexer_1_out), .out(s), .sel(c));  // open: en
endmodule
