// Logisim project ex04d.circ as structural Verilog: 1 circuit, main circuit main
module main (
  input  a,
  input  b,
  input  c,
  output Da
);

  wire and_1_out, and_2_out, not_1_out, not_2_out;

  not not_1 (not_1_out, a);
  and and_1 (and_1_out, not_1_out, b, c);
  not not_2 (not_2_out, b);
  and and_2 (and_2_out, a, c, not_2_out);
  or or_1 (Da, and_2_out, and_1_out);
endmodule
