// Logisim project ex02a.circ as structural Verilog: 1 circuit, main circuit main
module main (
  input  b,
  input  a,
  output s
);

  wire not_1_out;

  not not_1 (not_1_out, b);
  Multiplexer multiplexer_1 (.in0(not_1_out), .in1(b), .out(s), .sel(a));  // open: en
endmodule
