// Logisim project ex02b.circ as structural Verilog: 1 circuit, main circuit main
module main (
  input  a,
  input  b,
  input  c,
  output s
);

  wire nand_1_out, nand_2_out, nand_3_out, nand_4_out;

  nand nand_1 (nand_1_out, a, a);
  nand nand_2 (nand_2_out, b, b);
  nand nand_3 (nand_3_out, nand_1_out, b);
  nand nand_4 (nand_4_out, nand_2_out, c);
  nand nand_5 (s, nand_3_out, nand_4_out);
endmodule
