// Logisim project Guia_0804.circ as structural Verilog: 1 circuit, main circuit main
module main (
  input  A0,
  input  B3,
  input  A1,
  input  B2,
  input  B4,
  input  A2,
  input  B5,
  input  A4,
  input  B0,
  input  A3,
  input  B1,
  input  A5,
  output S
);

  wire xor_1_out, xor_2_out, xor_3_out, xor_4_out, xor_5_out, xor_6_out;

  xor xor_1 (xor_1_out, A0, B0);
  xor xor_2 (xor_2_out, A1, B1);
  xor xor_3 (xor_3_out, A2, B2);
  xor xor_4 (xor_4_out, A3, B3);
  xor xor_5 (xor_5_out, A4, B4);
  xor xor_6 (xor_6_out, A5, B5);
  or or_1 (S, xor_1_out, xor_2_out, xor_3_out, xor_4_out, xor_5_out, xor_6_out);
endmodule
