// Logisim project ex03.circ as structural Verilog: 1 circuit, main circuit main
module main (
  input  Clear,
  input  in_2,
  input  in_3,
  input  in_4,
  input  in_5,
  input  in_6,
  input  in_7,
  input  in_8,
  input  in_9,
  input  Enable,
  output out_11,
  output out_12,
  output out_13,
  output out_14,
  output out_15,
  output out_16,
  output out_17,
  output out_18
);

  wire clock_1_out, not_1_out, not_2_out, not_3_out, not_4_out, not_5_out, not_6_out, not_7_out, not_8_out,
       not_9_out;

  Clock clock_1 (.out(clock_1_out));
  not not_1 (not_1_out, in_2);
  J_K_Flip_Flop j_k_ff_1 (
    .J(in_2), .clk(clock_1_out), .K(not_1_out), .Q(out_11), .en(Enable), .reset(Clear));  // open: Qn, preset
  J_K_Flip_Flop j_k_ff_2 (
    .J(in_3), .clk(clock_1_out), .K(not_2_out), .Q(out_12), .en(Enable), .reset(Clear));  // open: Qn, preset
  not not_2 (not_2_out, in_3);
  not not_3 (not_3_out, in_4);
  J_K_Flip_Flop j_k_ff_3 (
    .J(in_4), .clk(clock_1_out), .K(not_3_out), .Q(out_13), .en(Enable), .reset(Clear));  // open: Qn, preset
  not not_4 (not_4_out, in_5);
  J_K_Flip_Flop j_k_ff_4 (
    .J(in_5), .clk(clock_1_out), .K(not_4_out), .Q(out_14), .en(Enable), .reset(Clear));  // open: Qn, preset
  not not_5 (not_5_out, Enable);
  not not_6 (not_6_out, in_6);
  J_K_Flip_Flop j_k_ff_5 (
    .J(in_6), .clk(clock_1_out), .K(not_6_out), .Q(out_15), .en(not_5_out), .reset(Clear));  // open: Qn, preset
  not not_7 (not_7_out, in_7);
  J_K_Flip_Flop j_k_ff_6 (
    .J(in_7), .clk(clock_1_out), .K(not_7_out), .Q(out_16), .en(not_5_out), .reset(Clear));  // open: Qn, preset
  not not_8 (not_8_out, in_8);
  J_K_Flip_Flop j_k_ff_7 (
    .J(in_8), .clk(clock_1_out), .K(not_8_out), .Q(out_17), .en(not_5_out), .reset(Clear));  // open: Qn, preset
  not not_9 (not_9_out, in_9);
  J_K_Flip_Flop j_k_ff_8 (
    .J(in_9), .clk(clock_1_out), .K(not_9_out), .Q(out_18), .en(not_5_out), .reset(Clear));  // open: Qn, preset

  // Notes on the sheet:
  //   Entradas de 8bits
  //   Saída total de 8bits
endmodule
