// Logisim project ex04.circ as structural Verilog: 1 circuit, main circuit main
module main (
  input  Clear,
  input  in_2,
  input  in_3,
  input  in_4,
  input  in_5,
  input  in_6,
  input  in_7,
  input  in_8,
  input  in_9,
  input  Enable,
  input  Enable_2,
  input  Clear_2,
  input  in_13,
  input  in_14,
  input  in_15,
  input  in_16,
  input  in_17,
  input  in_18,
  input  in_19,
  input  in_20,
  output out_21,
  output out_22,
  output out_23,
  output out_24,
  output out_25,
  output out_26,
  output out_27,
  output out_28,
  output out_29,
  output out_30,
  output out_31,
  output out_32,
  output out_33,
  output out_34,
  output out_35,
  output out_36
);

  wire clock_1_out, not_1_out, not_2_out, not_3_out, not_4_out, not_5_out, not_6_out, not_7_out, not_8_out,
       not_9_out, not_10_out, not_11_out, not_12_out, not_13_out, not_14_out, not_15_out, not_16_out,
       not_17_out, not_18_out;

  Clock clock_1 (.out(clock_1_out));
  not not_1 (not_1_out, in_2);
  not not_2 (not_2_out, in_13);
  J_K_Flip_Flop j_k_ff_1 (
    .J(in_2), .clk(clock_1_out), .K(not_1_out), .Q(out_21), .en(Enable), .reset(Clear));  // open: Qn, preset
  J_K_Flip_Flop j_k_ff_2 (
    .J(in_13), .clk(clock_1_out), .K(not_2_out), .Q(out_29), .en(Enable_2), .reset(Clear_2));  // open: Qn, preset
  J_K_Flip_Flop j_k_ff_3 (
    .J(in_3), .clk(clock_1_out), .K(not_3_out), .Q(out_22), .en(Enable), .reset(Clear));  // open: Qn, preset
  not not_3 (not_3_out, in_3);
  J_K_Flip_Flop j_k_ff_4 (
    .J(in_14), .clk(clock_1_out), .K(not_4_out), .Q(out_30), .en(Enable_2), .reset(Clear_2));  // open: Qn, preset
  not not_4 (not_4_out, in_14);
  not not_5 (not_5_out, in_4);
  not not_6 (not_6_out, in_15);
  J_K_Flip_Flop j_k_ff_5 (
    .J(in_4), .clk(clock_1_out), .K(not_5_out), .Q(out_23), .en(Enable), .reset(Clear));  // open: Qn, preset
  J_K_Flip_Flop j_k_ff_6 (
    .J(in_15), .clk(clock_1_out), .K(not_6_out), .Q(out_31), .en(Enable_2), .reset(Clear_2));  // open: Qn, preset
  not not_7 (not_7_out, in_5);
  not not_8 (not_8_out, in_16);
  J_K_Flip_Flop j_k_ff_7 (
    .J(in_5), .clk(clock_1_out), .K(not_7_out), .Q(out_24), .en(Enable), .reset(Clear));  // open: Qn, preset
  not not_9 (not_9_out, Enable);
  J_K_Flip_Flop j_k_ff_8 (
    .J(in_16), .clk(clock_1_out), .K(not_8_out), .Q(out_32), .en(Enable_2), .reset(Clear_2));  // open: Qn, preset
  not not_10 (not_10_out, Enable_2);
  not not_11 (not_11_out, in_6);
  not not_12 (not_12_out, in_17);
  J_K_Flip_Flop j_k_ff_9 (
    .J(in_6), .clk(clock_1_out), .K(not_11_out), .Q(out_25), .en(not_9_out), .reset(Clear));  // open: Qn, preset
  not not_13 (not_13_out, in_7);
  J_K_Flip_Flop j_k_ff_10 (
    .J(in_17), .clk(clock_1_out), .K(not_12_out), .Q(out_33), .en(not_10_out), .reset(Clear_2));  // open: Qn, preset
  not not_14 (not_14_out, in_18);
  J_K_Flip_Flop j_k_ff_11 (
    .J(in_7), .clk(clock_1_out), .K(not_13_out), .Q(out_26), .en(not_9_out), .reset(Clear));  // open: Qn, preset
  J_K_Flip_Flop j_k_ff_12 (
    .J(in_18), .clk(clock_1_out), .K(not_14_out), .Q(out_34), .en(not_10_out), .reset(Clear_2));  // open: Qn, preset
  not not_15 (not_15_out, in_8);
  not not_16 (not_16_out, in_19);
  J_K_Flip_Flop j_k_ff_13 (
    .J(in_8), .clk(clock_1_out), .K(not_15_out), .Q(out_27), .en(not_9_out), .reset(Clear));  // open: Qn, preset
  J_K_Flip_Flop j_k_ff_14 (
    .J(in_19), .clk(clock_1_out), .K(not_16_out), .Q(out_35), .en(not_10_out), .reset(Clear_2));  // open: Qn, preset
  not not_17 (not_17_out, in_9);
  J_K_Flip_Flop j_k_ff_15 (
    .J(in_20), .clk(clock_1_out), .K(not_18_out), .Q(out_36), .en(not_10_out), .reset(Clear_2));  // open: Qn, preset
  not not_18 (not_18_out, in_20);
  J_K_Flip_Flop j_k_ff_16 (
    .J(in_9), .clk(clock_1_out), .K(not_17_out), .Q(out_28), .en(not_9_out), .reset(Clear));  // open: Qn, preset

  // Notes on the sheet:
  //   Entradas de 8bits
  //   Entradas de 8bits
  //   Saída total de 8bits
endmodule
