// Logisim project ex01.circ as structural Verilog: 1 circuit, main circuit main
module main (
  input  \input ,
  input  clear,
  input  on,
  output out_4,
  output out_5,
  output out_6,
  output out_7,
  output out_8,
  output out_9
);

  wire clock_1_out;

  Clock clock_1 (.out(clock_1_out));
  J_K_Flip_Flop j_k_ff_1 (
    .J(\input ), .clk(clock_1_out), .K(\input ), .Q(out_9), .en(on), .reset(clear));  // open: Qn, preset
  J_K_Flip_Flop j_k_ff_2 (
    .J(\input ), .clk(out_9), .K(\input ), .Q(out_8), .en(on), .reset(clear));  // open: Qn, preset
  J_K_Flip_Flop j_k_ff_3 (
    .J(\input ), .clk(out_8), .K(\input ), .Q(out_7), .en(on), .reset(clear));  // open: Qn, preset
  J_K_Flip_Flop j_k_ff_4 (
    .J(\input ), .clk(out_7), .K(\input ), .Q(out_6), .en(on), .reset(clear));  // open: Qn, preset
  J_K_Flip_Flop j_k_ff_5 (
    .J(\input ), .clk(out_6), .K(\input ), .Q(out_5), .en(on), .reset(clear));  // open: Qn, preset
  J_K_Flip_Flop j_k_ff_6 (
    .J(\input ), .clk(out_5), .K(\input ), .Q(out_4), .en(on), .reset(clear));  // open: Qn, preset
endmodule
