// Logisim project Ex01.circ as structural Verilog: 1 circuit, main circuit main
module main (
  input  inp,
  input  clr,
  output out_3,
  output out_4,
  output out_5,
  output out_6,
  output out_7
);

  wire clock_1_out, d_ff_1_q, or_1_out, or_2_out, or_3_out, or_4_out;

  Clock clock_1 (.out(clock_1_out));
  or or_1 (or_1_out, clr, d_ff_1_q);
  D_Flip_Flop d_ff_1 (.clk(clock_1_out), .D(out_3), .Q(d_ff_1_q));  // open: Qn, preset, en, reset
  or or_2 (or_2_out, out_4, out_5);
  J_K_Flip_Flop j_k_ff_1 (
    .J(out_4), .clk(clock_1_out), .K(out_4), .Q(out_3), .reset(or_1_out));  // open: Qn, preset, en
  or or_3 (or_3_out, out_5, out_6);
  J_K_Flip_Flop j_k_ff_2 (
    .J(or_2_out), .clk(clock_1_out), .K(or_2_out), .Q(out_4), .reset(or_1_out));  // open: Qn, preset, en
  or or_4 (or_4_out, out_6, out_7);
  J_K_Flip_Flop j_k_ff_3 (
    .J(or_3_out), .clk(clock_1_out), .K(or_3_out), .Q(out_5), .reset(or_1_out));  // open: Qn, preset, en
  J_K_Flip_Flop j_k_ff_4 (
    .J(or_4_out), .clk(clock_1_out), .K(or_4_out), .Q(out_6), .reset(or_1_out));  // open: Qn, preset, en
  J_K_Flip_Flop j_k_ff_5 (
    .J(out_7), .clk(clock_1_out), .K(out_7), .Q(out_7), .preset(inp), .reset(or_1_out));  // open: Qn, en
endmodule
