// Logisim project ex04.circ as structural Verilog: 1 circuit, main circuit main
module main (
  input  inp,
  input  clr,
  output out_3,
  output out_4,
  output out_5,
  output out_6,
  output out_7
);

  wire clock_1_out, d_ff_1_q, d_ff_2_q, or_1_out, or_2_out, or_3_out, or_4_out, or_5_out;

  Clock clock_1 (.out(clock_1_out));
  D_Flip_Flop d_ff_1 (.clk(clock_1_out), .D(out_3), .Q(d_ff_1_q));  // open: Qn, preset, en, reset
  or or_1 (or_1_out, out_4, out_5);
  J_K_Flip_Flop j_k_ff_1 (
    .J(out_4), .clk(clock_1_out), .K(out_4), .Q(out_3), .reset(or_2_out));  // open: Qn, preset, en
  or or_2 (or_2_out, d_ff_1_q, clr);
  or or_3 (or_3_out, out_5, out_6);
  J_K_Flip_Flop j_k_ff_2 (
    .J(or_1_out), .clk(clock_1_out), .K(or_1_out), .Q(out_4), .reset(clr));  // open: Qn, preset, en
  or or_4 (or_4_out, out_6, out_7);
  J_K_Flip_Flop j_k_ff_3 (
    .J(or_3_out), .clk(clock_1_out), .K(or_3_out), .Q(out_5), .reset(clr));  // open: Qn, preset, en
  J_K_Flip_Flop j_k_ff_4 (
    .J(or_4_out), .clk(clock_1_out), .K(or_4_out), .Q(out_6), .reset(clr));  // open: Qn, preset, en
  D_Flip_Flop d_ff_2 (.clk(clock_1_out), .D(out_3), .Q(d_ff_2_q));  // open: Qn, preset, en, reset
  or or_5 (or_5_out, out_7, d_ff_2_q);
  J_K_Flip_Flop j_k_ff_5 (
    .J(or_5_out), .clk(clock_1_out), .K(or_5_out), .Q(out_7), .preset(inp), .reset(clr));  // open: Qn, en
endmodule
