// Logisim project ex05.circ as structural Verilog: 1 circuit, main circuit main
module main (
  input  inp,
  input  clr,
  input  in_3,
  input  in_4,
  input  in_5,
  input  in_6,
  input  in_7,
  output out_8,
  output out_9,
  output out_10,
  output out_11,
  output out_12
);

  wire clock_1_out, or_1_out, or_2_out, or_3_out;

  Clock clock_1 (.out(clock_1_out));
  J_K_Flip_Flop j_k_ff_1 (.J(in_3), .clk(clock_1_out), .K(inp), .Q(out_8), .reset(clr));  // open: Qn, preset, en
  or or_1 (or_1_out, out_10, in_4);
  J_K_Flip_Flop j_k_ff_2 (
    .J(or_1_out), .clk(clock_1_out), .K(or_1_out), .Q(out_9), .reset(clr));  // open: Qn, preset, en
  J_K_Flip_Flop j_k_ff_3 (
    .J(or_2_out), .clk(clock_1_out), .K(or_2_out), .Q(out_10), .reset(clr));  // open: Qn, preset, en
  or or_2 (or_2_out, out_11, in_5);
  or or_3 (or_3_out, out_12, in_6);
  J_K_Flip_Flop j_k_ff_4 (
    .J(or_3_out), .clk(clock_1_out), .K(or_3_out), .Q(out_11), .reset(clr));  // open: Qn, preset, en
  J_K_Flip_Flop j_k_ff_5 (.J(in_7), .clk(clock_1_out), .K(inp), .Q(out_12), .reset(clr));  // open: Qn, preset, en

  // Notes on the sheet:
  //   Para dar início insira a entrada que deseja, acione o botão inp, dê um pulso de clock e desligue o inp
endmodule
