// Logisim project ex05.circ as structural Verilog: 1 circuit, main circuit main
module main (
  input  in_1,
  output q3,
  output q2,
  output q1
);

  wire clock_1_out, not_1_out, not_2_out;

  Clock clock_1 (.out(clock_1_out));
  T_Flip_Flop t_ff_1 (.clk(clock_1_out), .T(in_1), .Q(q1));  // open: Qn, preset, reset, en
  not not_1 (not_1_out, q1);
  not not_2 (not_2_out, q2);
  T_Flip_Flop t_ff_2 (.clk(not_1_out), .T(in_1), .Q(q2));  // open: Qn, preset, reset, en
  T_Flip_Flop t_ff_3 (.clk(not_2_out), .T(in_1), .Q(q3));  // open: Qn, preset, reset, en
endmodule
