// Logisim project ex1Db.circ as structural Verilog: 1 circuit, main circuit main
module main (
  input  a,
  input  b,
  input  c
);

  wire and_1_out, and_2_out, and_3_out, clock_1_out, not_1_out, not_2_out, not_3_out, or_1_out;

  not not_1 (not_1_out, a);
  not not_2 (not_2_out, a);
  and and_1 (and_1_out, not_2_out, b);
  and and_2 (and_2_out, not_1_out, c);
  not not_3 (not_3_out, c);
  and and_3 (and_3_out, b, not_3_out);
  or or_1 (or_1_out, and_3_out, and_1_out, and_2_out);
  D_Flip_Flop d_ff_1 (.clk(clock_1_out), .D(or_1_out));  // open: Q, Qn, preset, en, reset
  Clock clock_1 (.out(clock_1_out));
endmodule
