// Logisim project ex2Ra.circ as structural Verilog: 1 circuit, main circuit main
module main (
  input  a,
  input  b,
  input  c
);

  wire and_1_out, clock_1_out, not_1_out;

  not not_1 (not_1_out, b);
  and and_1 (and_1_out, a, not_1_out, c);
  Clock clock_1 (.out(clock_1_out));
  S_R_Flip_Flop s_r_ff_1 (.S(and_1_out), .clk(clock_1_out), .R(and_1_out));  // open: Q, Qn, preset, reset, en
endmodule
