// Logisim project Ex02.circ as structural Verilog: 1 circuit, main circuit main
module main (
  input  x,
  input  y,
  output s
);

  wire and_1_out, not_1_out, not_2_out, not_3_out, or_1_out;

  not not_1 (not_1_out, x);
  not not_2 (not_2_out, y);
  and and_1 (and_1_out, not_2_out, y);
  or or_1 (or_1_out, x, not_1_out);
  not not_3 (not_3_out, or_1_out);
  and and_2 (s, and_1_out, not_3_out);

  // Notes on the sheet:
  //   w1
  //   w2
  //   w4
  //   w3
  //   w5
endmodule
