// Logisim project Ex05.circ as structural Verilog: 1 circuit, main circuit main
module main (
  input  a,
  input  b,
  output s
);

  wire nor_1_out, not_1_out, not_2_out, xnor_1_out;

  not not_1 (not_1_out, a);
  nor nor_1 (nor_1_out, not_1_out, not_2_out);
  not not_2 (not_2_out, b);
  xnor xnor_1 (xnor_1_out, a, b);
  nand nand_1 (s, xnor_1_out, nor_1_out);
endmodule
