// Logisim project ex04a.circ as structural Verilog: 1 circuit, main circuit main
module main (
  input  a,
  input  c,
  input  b,
  output Da
);

  wire and_1_out, and_2_out, and_3_out;

  and and_1 (and_1_out, a, c);
  and and_2 (and_2_out, a, b);
  and and_3 (and_3_out, c, b);
  or or_1 (Da, and_3_out, and_2_out, and_1_out);
endmodule
