// Logisim project ex05a.circ as structural Verilog: 1 circuit, main circuit main
module main (
  input  LOAD,
  input  clr,
  output out_3,
  output out_4,
  output out_5,
  output out_6
);

  wire clock_1_out, d_ff_1_q, not_1_out, or_1_out, xor_1_out, xor_2_out, xor_3_out;

  Clock clock_1 (.out(clock_1_out));
  xor xor_1 (xor_1_out, out_5, out_6);
  D_Flip_Flop d_ff_1 (.clk(clock_1_out), .D(not_1_out), .Q(d_ff_1_q));  // open: Qn, preset, en, reset
  not not_1 (not_1_out, out_6);
  J_K_Flip_Flop j_k_ff_1 (
    .J(xor_1_out), .clk(clock_1_out), .K(xor_1_out), .Q(out_6), .preset(or_1_out), .reset(clr));  // open: Qn, en
  or or_1 (or_1_out, LOAD, d_ff_1_q);
  xor xor_2 (xor_2_out, out_4, out_5);
  J_K_Flip_Flop j_k_ff_2 (
    .J(xor_2_out), .clk(clock_1_out), .K(xor_2_out), .Q(out_5), .preset(or_1_out), .reset(clr));  // open: Qn, en
  xor xor_3 (xor_3_out, out_3, out_4);
  J_K_Flip_Flop j_k_ff_3 (
    .J(xor_3_out), .clk(clock_1_out), .K(xor_3_out), .Q(out_4), .preset(or_1_out), .reset(clr));  // open: Qn, en
  J_K_Flip_Flop j_k_ff_4 (
    .J(out_3), .clk(clock_1_out), .K(out_3), .Q(out_3), .preset(or_1_out), .reset(clr));  // open: Qn, en
endmodule
