// Logisim project ex03a.circ as structural Verilog: 1 circuit, main circuit main
module main (
  input  b,
  input  a,
  input  d,
  output s
);

  wire and_1_out, and_2_out, not_1_out, not_2_out;

  not not_1 (not_1_out, b);
  not not_2 (not_2_out, a);
  and and_1 (and_1_out, not_1_out, a);
  and and_2 (and_2_out, not_2_out, d);
  or or_1 (s, and_1_out, and_2_out);
endmodule
