// Logisim project ex03b.circ as structural Verilog: 1 circuit, main circuit main
module main (
  input  a,
  input  b,
  input  c,
  input  d,
  output s
);

  wire and_1_out, and_2_out, and_3_out, not_1_out, not_2_out, not_3_out, or_1_out;

  not not_1 (not_1_out, a);
  not not_2 (not_2_out, b);
  not not_3 (not_3_out, c);
  // NOT_Gate not_4 has open pins: in=d, out=open
  and and_1 (and_1_out, not_1_out, not_3_out, d);
  and and_2 (and_2_out, a, not_2_out);
  and and_3 (and_3_out, d, not_2_out);
  or or_1 (or_1_out, and_1_out, and_2_out);
  or or_2 (s, or_1_out, and_3_out);
endmodule
