// Logisim project ex04.circ as structural Verilog: 1 circuit, main circuit main
module main (
  input  a,
  input  b,
  input  c,
  output s
);

  wire and_1_out, not_1_out, or_1_out;

  not not_1 (not_1_out, a);
  and and_1 (and_1_out, b, c);
  or or_1 (or_1_out, not_1_out, and_1_out);
  not not_2 (s, or_1_out);
endmodule
