// Logisim project ex05.circ as structural Verilog: 1 circuit, main circuit main
module main (
  output out_1,
  output out_2
);

  wire clock_1_out, j_k_ff_1_qn, j_k_ff_2_qn;

  Clock clock_1 (.out(clock_1_out));
  J_K_Flip_Flop j_k_ff_1 (
    .J(j_k_ff_2_qn), .clk(clock_1_out), .K(out_2), .Q(out_1), .Qn(j_k_ff_1_qn));  // open: preset, en, reset
  J_K_Flip_Flop j_k_ff_2 (
    .J(out_1), .clk(clock_1_out), .K(j_k_ff_1_qn), .Q(out_2), .Qn(j_k_ff_2_qn));  // open: preset, en, reset
endmodule
