// Logisim project Tp04.circ as structural Verilog
module ULA (
  input  A0,
  input  A1,
  input  A2,
  input  A3,
  input  B0,
  input  B1,
  input  B2,
  input  B3,
  input  S0,
  input  S1,
  input  S2,
  input  S3
);

  wire not_1_out, not_2_out, not_3_out, not_4_out, not_5_out, not_6_out, not_7_out, not_8_out, not_9_out,
       not_10_out, not_11_out, not_12_out, not_13_out, not_14_out, not_15_out, not_16_out, not_17_out,
       not_18_out, not_19_out, not_21_out, not_22_out, not_23_out, not_24_out, not_25_out, not_26_out,
       not_27_out, not_28_out, not_29_out, not_30_out, not_31_out, not_32_out, not_33_out, not_34_out,
       not_35_out;

  not not_1 (not_1_out, S0);
  not not_2 (not_2_out, S1);
  not not_3 (not_3_out, S2);
  not not_4 (not_4_out, S3);
  not not_5 (not_5_out, S0);
  not not_6 (not_6_out, S1);
  not not_7 (not_7_out, S2);
  not not_8 (not_8_out, S0);
  not not_9 (not_9_out, S1);
  not not_10 (not_10_out, S3);
  not not_11 (not_11_out, S0);
  not not_12 (not_12_out, S1);
  not not_13 (not_13_out, S0);
  not not_14 (not_14_out, S2);
  not not_15 (not_15_out, S3);
  not not_16 (not_16_out, S0);
  not not_17 (not_17_out, S2);
  not not_18 (not_18_out, S3);
  not not_19 (not_19_out, S0);
  // NOT_Gate not_20 has open pins: in=S2, out=open
  not not_21 (not_21_out, S0);
  not not_22 (not_22_out, S3);
  not not_23 (not_23_out, S0);
  not not_24 (not_24_out, S1);
  not not_25 (not_25_out, S2);
  not not_26 (not_26_out, S3);
  not not_27 (not_27_out, S1);
  not not_28 (not_28_out, S2);
  not not_29 (not_29_out, S1);
  not not_30 (not_30_out, S3);
  not not_31 (not_31_out, S1);
  not not_32 (not_32_out, S2);
  not not_33 (not_33_out, S3);
  not not_34 (not_34_out, S2);
  not not_35 (not_35_out, S3);
  // AND_Gate and_1 has open pins: in1=not_1_out, in2=not_2_out, in3=not_3_out, in4=not_4_out, out=open
  // AND_Gate and_2 has open pins: in1=not_5_out, in2=not_6_out, in3=not_7_out, in4=S3, out=open
  // AND_Gate and_3 has open pins: in1=not_8_out, in2=not_9_out, in3=S2, in4=not_10_out, out=open
  // AND_Gate and_4 has open pins: in1=not_11_out, in2=not_12_out, in3=S2, in4=S3, out=open
  // AND_Gate and_5 has open pins: in1=not_13_out, in2=S1, in3=not_14_out, in4=not_15_out, out=open
  // AND_Gate and_6 has open pins: in1=not_16_out, in2=S1, in3=not_17_out, in4=not_18_out, out=open
  // AND_Gate and_7 has open pins: in1=not_19_out, in2=S1, in4=S3, out=open
  // AND_Gate and_8 has open pins: in1=not_21_out, in2=S1, in3=S2, in4=not_22_out, out=open
  // AND_Gate and_9 has open pins: in1=not_23_out, in2=S1, in3=S2, in4=S3, out=open
  // AND_Gate and_10 has open pins: in1=S0, in2=not_24_out, in3=not_25_out, in4=not_26_out, out=open
  // AND_Gate and_11 has open pins: in1=S0, in2=not_27_out, in3=not_28_out, in4=S3, out=open
  // AND_Gate and_12 has open pins: in1=S0, in2=not_29_out, in3=S2, in4=not_30_out, out=open
  // AND_Gate and_13 has open pins: in1=S0, in2=not_31_out, in3=S2, in4=S3, out=open
  // AND_Gate and_14 has open pins: in1=S0, in2=S1, in3=not_32_out, in4=not_33_out, out=open
  // AND_Gate and_15 has open pins: in1=S0, in2=S1, in3=not_34_out, in4=S3, out=open
  // AND_Gate and_16 has open pins: in1=S0, in2=S1, in3=S2, in4=not_35_out, out=open
  // AND_Gate and_17 has open pins: in1=S0, in2=S1, in3=S2, in4=S3, out=open
endmodule
