// Logisim project TP02.circ as structural Verilog: 5 circuits, main circuit main
module main (
  input  Binvert,
  input  b3,
  input  b2,
  input  b1,
  input  b0,
  input  a3,
  input  a2,
  input  a1,
  input  a0,
  input  op1,
  input  op0,
  output s1,
  output s0,
  output s3,
  output s2,
  output Cout
);

  wire ula_1_carryout, ula_2_carryout, ula_3_carryout;

  ULA ula_1 (.a(a0), .b(b0), .s(s0), .Binvert(Binvert), .Cin(Binvert), .CarryOut(ula_1_carryout), .op0(op1), .op1(op0));
  ULA ula_2 (
    .a(a1), .b(b1), .s(s1), .Binvert(Binvert), .Cin(ula_1_carryout), .CarryOut(ula_2_carryout), .op0(op1),
    .op1(op0));
  ULA ula_3 (
    .a(a2), .b(b2), .s(s2), .Binvert(Binvert), .Cin(ula_2_carryout), .CarryOut(ula_3_carryout), .op0(op1),
    .op1(op0));
  ULA ula_4 (.a(a3), .b(b3), .s(s3), .Binvert(Binvert), .Cin(ula_3_carryout), .CarryOut(Cout), .op0(op1), .op1(op0));

  // Notes on the sheet:
  //   RESULTADO:
endmodule

module binvert (
  input  b0,
  input  b1,
  output s0
);

  // XOR_Gate xor_1: pin names not known; wires that end beside it: b0, b1, s0
endmodule

module soma (
  input  Ci0,
  input  A0,
  input  B0,
  output S0,
  output Co0
);

  wire and_1_out, and_2_out, xor_1_out;

  xor xor_1 (xor_1_out, A0, B0);
  and and_1 (and_1_out, A0, B0);
  xor xor_2 (S0, xor_1_out, Ci0);
  and and_2 (and_2_out, xor_1_out, Ci0);
  or or_1 (Co0, and_2_out, and_1_out);

  // Notes on the sheet:
  //   somador completo de 1 bit
endmodule

module \Operações  (
  input  m,
  input  n,
  input  o,
  input  p,
  input  op0,
  input  op1,
  output s0
);

  wire and_1_out, and_2_out, and_3_out, and_4_out, not_1_out, not_2_out, not_3_out, not_4_out;

  not not_1 (not_1_out, op0);
  and and_1 (and_1_out, m, not_1_out, not_2_out);
  not not_2 (not_2_out, op1);
  and and_2 (and_2_out, n, not_3_out, op1);
  not not_3 (not_3_out, op0);
  and and_3 (and_3_out, o, op0, not_4_out);
  not not_4 (not_4_out, op1);
  and and_4 (and_4_out, p, op0, op1);
  or or_1 (s0, and_1_out, and_2_out, and_3_out, and_4_out);
endmodule

module ULA (
  input  Cin,
  input  Binvert,
  input  a,
  input  b,
  input  op0,
  input  op1,
  output s,
  output CarryOut
);

  wire and_1_out, multiplexer_1_out, not_1_out, not_2_out, or_1_out, or_2_out, soma_1_s0;

  Multiplexer #(.enable("false")) multiplexer_1 (.in0(b), .in1(not_1_out), .out(multiplexer_1_out), .sel(Binvert));
  not not_1 (not_1_out, b);
  or or_1 (or_1_out, Binvert, Cin);
  soma soma_1 (.Ci0(or_1_out), .A0(a), .S0(soma_1_s0), .B0(multiplexer_1_out), .Co0(CarryOut));
  and and_1 (and_1_out, a, b);
  or or_2 (or_2_out, a, b);
  not not_2 (not_2_out, a);
  \Operações  \operações_1  (.m(and_1_out), .n(or_2_out), .o(not_2_out), .p(soma_1_s0), .s0(s), .op0(op0), .op1(op1));

  // Notes on the sheet:
  //   OPERAÇÕES
endmodule
